# Fritzing sketch led-corridor (saved by Fritzing 0.9.9b)

parts:
  U1 = NodeMCU V3.0
  Part1 = TXB0108 8-channel Bi-directional Logic Level Converter
  Power_plug1 = Power plug
  M1 = RioRand LM2596
  R1 = Resistor [tolerance=±5% resistance=330 package="0603 [SMD]"]
  C1 = Capacitor Polarized [package=cpol-radial-1000uf-25v]
  R2 = Resistor [tolerance=±5% resistance=10k package="0603 [SMD]"]
  U2 = WS2812 RGB LED strip

nets:
  N1: U1.D1, Part1.A1
  GND: U1.GND, Part1.GND, M1.Pin_4, C1.-, U2.GND
  VIN: U1.Vin, Part1.VCCB, M1.Pin_3, C1.+, U2.VCC
  N2: Part1.B1, R2.Pin_1
  N3: Part1.OE, R1.Pin_1
  N4: Part1.VCCA, R1.Pin_0
  N5: Power_plug1.GND, M1.Pin_2
  N6: Power_plug1.VCC, M1.Pin_1
  N7: R2.Pin_0, U2.DIN

custom parts:
  NodeMCU V3.0: NodeMcu V3 Lua WIFI Development Board
  TXB0108 8-channel Bi-directional Logic Level Converter: Because the Arduino (and Basic Stamp) are 5V devices, and most modern sensors, displays, flash cards and modes are 3.3V-only, many makers find that they need to perform level shifting/conversion to protect the 3.3V device from 5V. Although one can use resistors to make a divider, for high speed transfers, the resistors can add a lot of slew and cause havoc that is tough to debug. For that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
  WS2812 RGB LED strip: WS2812 strip
